# Fritzing sketch Sketch (saved by Fritzing 0.9.3b)
breadboards: 1

parts:
  Part1 = Arduino Uno (Rev3)
  S1 = Pushbutton [package="[THT]"]
  R1 = Resistor [tolerance=±5% resistance=220 package=THT]
  S2 = Pushbutton [package="[THT]"]
  R2 = Resistor [tolerance=±5% resistance=220 package=THT]
  R3 = Photocell (LDR) [package=THT]
  R4 = Resistor [tolerance=±5% resistance=220 package=THT]
  S3 = Pushbutton [package="[THT]"]
  S4 = Pushbutton [package="[THT]"]
  S5 = Pushbutton [package="[THT]"]
  R5 = Resistor [tolerance=±5% resistance=220 package=THT]
  R6 = Resistor [tolerance=±5% resistance=220 package=THT]
  R7 = Resistor [tolerance=±5% resistance=220 package=THT]

nets:
  N1: Part1.D8, S1.Pin_1, S1.Pin_2, R1.Pin_0
  N2: Part1.D9_PWM, S2.Pin_1, S2.Pin_2, R2.Pin_0
  N3: Part1.D11_PWM/MOSI, S3.Pin_1, S3.Pin_2, R5.Pin_0
  N4: Part1.D12/MISO, S4.Pin_1, S4.Pin_2, R6.Pin_0
  N5: Part1.D13/SCK, S5.Pin_1, S5.Pin_2
  N6: Part1.D5_PWM, R3.pin_1, R4.Pin_0
  N7: Part1.5V, S1.Pin_3, S1.Pin_4, S2.Pin_3, S2.Pin_4, R3.pin_0, S3.Pin_3, S3.Pin_4, S4.Pin_3, S4.Pin_4, S5.Pin_3, S5.Pin_4
  N8: Part1.GND, R4.Pin_1, R5.Pin_1, R6.Pin_1, R7.Pin_1
